# Fritzing sketch RelayBoard (saved by Fritzing 0.9.2b)
breadboards: 1

parts:
  Part1 = Arduino Mega 2560 (Rev3)
  J1 = Power Jack [package=power_jack_pth_lock]
  4_Relay_Module1 = OPENMolo 4 Relay breakout board
  M1 = DC Motor
  M2 = DC Motor
  S1 = Tilt Switch [package=THT]
  J2 = Power Jack [package=power_jack_pth_lock]
  U1 = TOUCH [package=touch2]
  R1 = Resistor [tolerance=±5% resistance=220 package=THT]
  R2 = Resistor [tolerance=±5% resistance=220 package=THT]
  LED1 = LED - 5mm [color="Red (633nm)" package="5 mm [THT]"]
  LED2 = LED - 5mm [color="Red (633nm)" package="5 mm [THT]"]
  S2 = Tilt Switch [package=THT]
  R3 = Resistor [tolerance=±5% resistance=220 package=THT]
  LED3 = LED - 5mm [color="Red (633nm)" package="5 mm [THT]"]

nets:
  N1: Part1.D9_PWM, S2.Pin_1
  N2: Part1.D8_PWM, S1.Pin_1
  N3: Part1.5V, 4_Relay_Module1.P_VCC
  N4: Part1.GND, S1.Pin_2, LED1.cathode, LED2.cathode, S2.Pin_2
  N5: Part1.D2_PWM, 4_Relay_Module1.E1, R1.Pin_0
  N6: Part1.D3_PWM, 4_Relay_Module1.E2, R2.Pin_0
  N7: Part1.D4_PWM, 4_Relay_Module1.E3, R3.Pin_0
  N8: Part1.D5_PWM, 4_Relay_Module1.E4
  N9: J1.GNDBREAK, 4_Relay_Module1.P_GND, M1.pin_1, M2.pin_1
  N10: J1.PWR, 4_Relay_Module1.PW_Rel_3, 4_Relay_Module1.PW_Rel_4
  N11: 4_Relay_Module1.PW_Rel_1, J2.PWR
  N12: 4_Relay_Module1.NO_Rel_1, U1.T1
  N13: 4_Relay_Module1.NO_Rel_3, M1.pin_2
  N14: 4_Relay_Module1.NO_Rel_4, M2.pin_2
  N15: J2.GNDBREAK, U1.T2
  N16: R1.Pin_1, LED1.anode
  N17: R2.Pin_1, LED2.anode
  N18: R3.Pin_1, LED3.anode

notes:
  First schematics to run the pump with the Arduino.
  Water Level sensors
  Fish Tank Pump
  Plant Tank Pump
  12V Power
  Arduino Power
  Ultrasonic Fogger
  24V Power
  LED Strip
  Relay Sim Led

custom parts:
  OPENMolo 4 Relay breakout board: Módulo de 8 relés de 10A optoaislados pensado para desarrollos rápidos basadon en microcontroladores o microcomputadoras. Estos módulos son diseñados con especial cuidado tanto en sus capacidades aisladoras para preservar equipos de mayor valor asi como en las fijaciones para evitar problemas a la hora de armar un prototipo o de fijarlo en un tablero definitivo. Una importante característica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
