# Fritzing sketch pump (saved by Fritzing 0.9.2b)
breadboards: 1

parts:
  Q1 = NPN-Transistor [package="TO92 [THT]"]
  R1 = Resistor [tolerance=±5% resistance=560 package=THT]
  M1 = DC Motor
  D1 = Rectifier Diode [part_number=1N4001 package="300 mil [THT]"]

nets:
  N1: Q1.B, R1.Pin_1
  N2: M1.pin_2, D1.anode
  5V: D1.cathode

notes:
  First schematics to ru the pump with the Arduino.
